// Logisim project nand2tetris.circ as structural Verilog
module Not (
  input  Input,
  output Output
);

  nand nand_1 (Output, Input, Input);
endmodule

module And (
  input  in_1,
  input  in_2,
  output out_3
);

  wire nand_1_out;

  nand nand_1 (nand_1_out, in_1, in_2);
  Not not_1 (.Input(nand_1_out), .Output(out_3));
endmodule
